# Fritzing sketch ValloxSensor (saved by Fritzing 0.9.1b)
breadboards: 1

parts:
  Bauteil1 = Arduino Mega 2560 (Rev3)
  U1 = MAX485 [package=dil08]
  U2 = MAX485 [package=dil08]
  J1 = Screw terminal - 2 pins [package=THT]
  R1 = Resistor [tolerance=±5% resistance=120 package=THT]
  Bauteil2 = NRF24L01
  S1 = Pushbutton [package="[THT]"]
  C1 = Electrolytic Capacitor [capacitance=47µF package="100 mil [THT, electrolytic]"]

nets:
  N1: Bauteil1.D19/RX1, U1.RO
  N2: Bauteil1.D18/TX1, U1.DI
  N3: Bauteil1.D17_PWM/RX2, U2.RO
  N4: Bauteil1.D16_PWM/TX2, U2.DI
  GND: Bauteil1.GND, U1.RE, U1.DE, U2.GND, Bauteil2.GND, S1.Pin_3, S1.Pin_4, C1.-
  3V3: Bauteil1.3V3, Bauteil2.VCC
  VCC: Bauteil1.5V, U1.VCC, U2.VCC, C1.+
  N5: Bauteil1.D2_PWM, Bauteil2.IRQ
  N6: Bauteil1.D3_PWM, Bauteil2.CE
  N7: Bauteil1.D4_PWM, Bauteil2.CSN
  N8: Bauteil1.D5_PWM, U2.RE, U2.DE
  N9: Bauteil1.D6_PWM, S1.Pin_1, S1.Pin_2
  N10: Bauteil1.D50, Bauteil2.MISO
  N11: Bauteil1.D51, Bauteil2.MOSI
  N12: Bauteil1.D52, Bauteil2.SCK
  N13: U1.A, U2.A, J1.pin2, R1.Pin_1
  N14: U1.B, U2.B, J1.pin1, R1.Pin_0

notes:
  8 x Pullup 10k
  20k A VCC
  20k B GND
  are missing
  TX
  RX
  Vallox RS485
  BoostSwitch
